// Logisim project Taller 1.circ as structural Verilog
module SS1b (
  input  In0,
  input  In1,
  output S,
  output Cout
);

  xor xor_1 (S, In0, In1);
  and and_1 (Cout, In0, In1);
endmodule

module sc1b (
  input  in0,
  input  in1,
  input  Cin,
  output S,
  output Cout
);

  wire ss1b_1_cout, ss1b_1_s, ss1b_2_cout;

  SS1b ss1b_1 (.In0(in0), .In1(in1), .S(ss1b_1_s), .Cout(ss1b_1_cout));
  SS1b ss1b_2 (.In0(ss1b_1_s), .In1(Cin), .S(S), .Cout(ss1b_2_cout));
  or or_1 (Cout, ss1b_2_cout, ss1b_1_cout);
endmodule

module S4b (
  input  a0,
  input  a1,
  input  a2,
  input  a3,
  input  b0,
  input  b1,
  input  b2,
  input  b3,
  output s0,
  output s1,
  output s2,
  output s3,
  output Cout
);

  wire sc1b_1_cout, sc1b_2_cout, ss1b_1_cout;

  SS1b ss1b_1 (.In0(a0), .In1(b0), .S(s0), .Cout(ss1b_1_cout));
  sc1b sc1b_1 (.in0(ss1b_1_cout), .in1(a1), .Cin(b1), .S(s1), .Cout(sc1b_1_cout));
  sc1b sc1b_2 (.in0(sc1b_1_cout), .in1(a2), .Cin(b2), .S(s2), .Cout(sc1b_2_cout));
  sc1b sc1b_3 (.in0(sc1b_2_cout), .in1(a3), .Cin(b3), .S(s3), .Cout(Cout));
endmodule

module Comparador_con_cero_4_bits (
  input  in_1,
  input  in_2,
  input  in_3,
  input  in_4,
  output out_5
);

  wire or_1_out, or_2_out, or_3_out;

  or or_1 (or_1_out, in_1, in_2);
  or or_2 (or_2_out, in_3, in_4);
  or or_3 (or_3_out, or_1_out, or_2_out);
  not not_1 (out_5, or_3_out);
endmodule

module Sum_4_bits_con_flags (
  input  a0,
  input  a1,
  input  a2,
  input  a3,
  input  b0,
  input  b1,
  input  b2,
  input  b3,
  output s0,
  output s1,
  output s2,
  output s3,
  output C,
  output N,
  output Z,
  output V
);

  wire and_1_out, and_2_out, and_3_out, and_4_out, not_1_out, not_2_out, not_3_out;

  S4b s4b_1 (
    .a0(a0), .a1(a1), .a2(a2), .a3(a3), .b0(b0), .b1(b1), .b2(b2), .b3(b3), .s0(s0), .s1(s1), .s2(s2),
    .s3(N), .Cout(C));
  not not_1 (not_1_out, a3);
  not not_2 (not_2_out, b3);
  Comparador_con_cero_4_bits comparador_con_cero_4_bits_1 (.in_1(s0), .in_2(s1), .in_3(s2), .in_4(N), .out_5(Z));
  and and_1 (and_1_out, not_1_out, not_2_out);
  and and_2 (and_2_out, a3, b3);
  not not_3 (not_3_out, N);
  and and_3 (and_3_out, N, and_1_out);
  and and_4 (and_4_out, not_3_out, and_2_out);
  or or_1 (V, and_3_out, and_4_out);

  assign s3 = N;
endmodule

module Inversor_4_bits (
  input  in_1,
  input  in_2,
  input  in_3,
  input  in_4,
  output out_5,
  output out_6,
  output out_7,
  output out_8
);

  not not_1 (out_5, in_1);
  not not_2 (out_6, in_2);
  not not_3 (out_7, in_3);
  not not_4 (out_8, in_4);
endmodule

module Incrementador_4_bits (
  input  a0,
  input  a1,
  input  a2,
  input  a3,
  output s0,
  output s1,
  output s2,
  output s3,
  output C,
  output N,
  output Z,
  output V
);

  Sum_4_bits_con_flags sum_4_bits_con_flags_1 (
    .a0(a0), .a1(a1), .a2(a2), .a3(a3), .b0(1'b1), .b1(1'b0), .b2(1'b0), .b3(1'b0), .s0(s0), .s1(s1),
    .s2(s2), .s3(s3), .C(C), .N(N), .Z(Z), .V(V));
endmodule

module Restador_4_bits (
  input  a0,
  input  a1,
  input  a2,
  input  a3,
  input  b0,
  input  b1,
  input  b2,
  input  b3,
  output s0,
  output s1,
  output s2,
  output s3,
  output C,
  output N,
  output Z,
  output V
);

  wire incrementador_4_bits_1_s0, incrementador_4_bits_1_s1, incrementador_4_bits_1_s2,
       incrementador_4_bits_1_s3, incrementador_4_bits_1_v, inversor_4_bits_1_out_5, inversor_4_bits_1_out_6,
       inversor_4_bits_1_out_7, inversor_4_bits_1_out_8, sum_4_bits_con_flags_1_v;

  Inversor_4_bits inversor_4_bits_1 (
    .in_1(b0), .in_2(b1), .in_3(b2), .in_4(b3), .out_5(inversor_4_bits_1_out_5),
    .out_6(inversor_4_bits_1_out_6), .out_7(inversor_4_bits_1_out_7), .out_8(inversor_4_bits_1_out_8));
  Incrementador_4_bits incrementador_4_bits_1 (
    .a0(inversor_4_bits_1_out_5), .a1(inversor_4_bits_1_out_6), .a2(inversor_4_bits_1_out_7),
    .a3(inversor_4_bits_1_out_8), .s0(incrementador_4_bits_1_s0), .s1(incrementador_4_bits_1_s1),
    .s2(incrementador_4_bits_1_s2), .s3(incrementador_4_bits_1_s3), .V(incrementador_4_bits_1_v));  // open: C, N, Z
  Sum_4_bits_con_flags sum_4_bits_con_flags_1 (
    .a0(a0), .a1(a1), .a2(a2), .a3(a3), .b0(incrementador_4_bits_1_s0), .b1(incrementador_4_bits_1_s1),
    .b2(incrementador_4_bits_1_s2), .b3(incrementador_4_bits_1_s3), .s0(s0), .s1(s1), .s2(s2), .s3(s3),
    .C(C), .N(N), .Z(Z), .V(sum_4_bits_con_flags_1_v));
  or or_1 (V, sum_4_bits_con_flags_1_v, incrementador_4_bits_1_v);
endmodule
