// Logisim project taller2-alu.circ as structural Verilog: 5 circuits, main circuit 3estados
module _3estados (
  input  A,
  input  A_en,
  input  B,
  input  B_en,
  input  C,
  input  C_en,
  output Res
);

  assign Res = A_en ? A : 1'bz;  // Controlled_Buffer controlled_buffer_1
  assign Res = B_en ? B : 1'bz;  // Controlled_Buffer controlled_buffer_2
  assign Res = C_en ? C : 1'bz;  // Controlled_Buffer controlled_buffer_3

  // Notes on the sheet:
  //   Ejercicio 1
endmodule

module ej_2 (
  input  W_0,
  input  en_0,
  input  W_1,
  input  en_1,
  input  clk,
  input  W_2,
  input  en_2,
  input  Force_input,
  input  en_force_input,
  output R0,
  output BUS,
  output R1,
  output R2
);

  assign BUS = en_force_input ? Force_input : 1'bz;  // Controlled_Buffer controlled_buffer_1
  registro_salida_restringida registro_salida_restringida_1 (
    .clk(clk), .in(BUS), .out_debug(R0), .out(BUS), .w(W_0), .en_out(en_0));
  registro_salida_restringida registro_salida_restringida_2 (
    .clk(clk), .in(BUS), .out_debug(R1), .out(BUS), .w(W_1), .en_out(en_1));
  registro_salida_restringida registro_salida_restringida_3 (
    .clk(clk), .in(BUS), .out_debug(R2), .out(BUS), .w(W_2), .en_out(en_2));

  // Notes on the sheet:
  //   Ejercicio 2
endmodule

module registro_salida_restringida (
  input  clk,
  input  in,
  input  w,
  input  en_out,
  output out_debug,
  output out
);

  D_Flip_Flop d_ff_1 (.clk(clk), .D(in), .Q(out_debug), .en(w));  // open: Qn, preset, reset
  assign out = en_out ? out_debug : 1'bz;  // Controlled_Buffer controlled_buffer_1

  // Notes on the sheet:
  //   Registro 1b salida restringida
endmodule

module ej_3 (
  input  in_1,
  input  W_0,
  input  ADD_en,
  input  en_0,
  input  W_OP1,
  input  W_1,
  input  en_1,
  input  SUB_en,
  input  W_2,
  input  W_OP1_2,
  input  en_2,
  input  W_3,
  input  en_3,
  input  [3:0] Force_input,
  input  en_force_input,
  output out_16,
  output out_17
);

  wire not_1_out;
  wire [3:0] adder_1_out, controlled_buffer_1_out, registro_4b_salida_restringida_1_out,
       registro_4b_salida_restringida_1_out4_d, registro_4b_salida_restringida_2_out4_d,
       registro_4b_salida_restringida_3_out4_d, registro_4b_salida_restringida_4_out4_d,
       registro_4b_salida_restringida_5_out, registro_4b_salida_restringida_5_out4_d,
       registro_4b_salida_restringida_6_out, registro_4b_salida_restringida_6_out4_d,
       registro_4b_salida_restringida_7_out4_d, registro_4b_salida_restringida_8_out4_d, subtractor_1_out;

  registro_4b_salida_restringida registro_4b_salida_restringida_1 (
    .In_4(controlled_buffer_1_out), .clk(in_1), .w(W_0), .en(en_0),
    .out4_d(registro_4b_salida_restringida_1_out4_d), .out(registro_4b_salida_restringida_1_out));
  registro_4b_salida_restringida registro_4b_salida_restringida_2 (
    .In_4(controlled_buffer_1_out), .clk(in_1), .w(W_1), .en(en_1),
    .out4_d(registro_4b_salida_restringida_2_out4_d), .out(registro_4b_salida_restringida_1_out));
  registro_4b_salida_restringida registro_4b_salida_restringida_3 (
    .In_4(controlled_buffer_1_out), .clk(in_1), .w(W_2), .en(en_2),
    .out4_d(registro_4b_salida_restringida_3_out4_d), .out(registro_4b_salida_restringida_1_out));
  registro_4b_salida_restringida registro_4b_salida_restringida_4 (
    .In_4(controlled_buffer_1_out), .clk(in_1), .w(W_3), .en(en_3),
    .out4_d(registro_4b_salida_restringida_4_out4_d), .out(registro_4b_salida_restringida_1_out));
  assign controlled_buffer_1_out = en_force_input ? Force_input : 4'bz;  // Controlled_Buffer controlled_buffer_1
  Hex_Digit_Display hex_digit_display_1 (.value(registro_4b_salida_restringida_1_out4_d));  // open: dp
  Hex_Digit_Display hex_digit_display_2 (.value(registro_4b_salida_restringida_2_out4_d));  // open: dp
  Hex_Digit_Display hex_digit_display_3 (.value(registro_4b_salida_restringida_3_out4_d));  // open: dp
  Hex_Digit_Display hex_digit_display_4 (.value(registro_4b_salida_restringida_4_out4_d));  // open: dp
  Hex_Digit_Display hex_digit_display_5 (.value(registro_4b_salida_restringida_1_out));  // open: dp
  Hex_Digit_Display hex_digit_display_6 (.value(registro_4b_salida_restringida_5_out4_d));  // open: dp
  registro_4b_salida_restringida registro_4b_salida_restringida_5 (
    .In_4(registro_4b_salida_restringida_1_out), .clk(in_1), .w(W_OP1), .en(1'b1),
    .out4_d(registro_4b_salida_restringida_5_out4_d), .out(registro_4b_salida_restringida_5_out));
  Hex_Digit_Display hex_digit_display_7 (.value(registro_4b_salida_restringida_6_out4_d));  // open: dp
  registro_4b_salida_restringida registro_4b_salida_restringida_6 (
    .In_4(registro_4b_salida_restringida_1_out), .clk(in_1), .w(W_OP1_2), .en(1'b1),
    .out4_d(registro_4b_salida_restringida_6_out4_d), .out(registro_4b_salida_restringida_6_out));
  Adder #(.width(4)) adder_1 (
    .a(registro_4b_salida_restringida_5_out), .b(registro_4b_salida_restringida_6_out), .out(adder_1_out),
    .cin(1'b0), .cout(out_16));
  not not_1 (not_1_out, in_1);
  Subtractor #(.width(4)) subtractor_1 (
    .a(registro_4b_salida_restringida_5_out), .b(registro_4b_salida_restringida_6_out),
    .out(subtractor_1_out), .bin(1'b0), .bout(out_17));
  Hex_Digit_Display hex_digit_display_8 (.value(controlled_buffer_1_out));  // open: dp
  Hex_Digit_Display hex_digit_display_9 (.value(registro_4b_salida_restringida_7_out4_d));  // open: dp
  registro_4b_salida_restringida registro_4b_salida_restringida_7 (
    .In_4(adder_1_out), .clk(not_1_out), .w(1'b1), .en(ADD_en),
    .out4_d(registro_4b_salida_restringida_7_out4_d), .out(controlled_buffer_1_out));
  Hex_Digit_Display hex_digit_display_10 (.value(registro_4b_salida_restringida_8_out4_d));  // open: dp
  registro_4b_salida_restringida registro_4b_salida_restringida_8 (
    .In_4(subtractor_1_out), .clk(not_1_out), .w(1'b1), .en(SUB_en),
    .out4_d(registro_4b_salida_restringida_8_out4_d), .out(controlled_buffer_1_out));

  // Other names for the same wires on the sheet: clk = in_1

  // Notes on the sheet:
  //   Ejercicio 3
  //   Bus 1
  //   Bus 2
endmodule

module registro_4b_salida_restringida (
  input  [3:0] In_4,
  input  clk,
  input  w,
  input  en,
  output [3:0] out4_d,
  output [3:0] out
);

  D_Flip_Flop d_ff_1 (.clk(clk), .D(In_4[0]), .Q(out4_d[0]), .en(w));  // open: Qn, preset, reset
  D_Flip_Flop d_ff_2 (.clk(clk), .D(In_4[1]), .Q(out4_d[1]), .en(w));  // open: Qn, preset, reset
  D_Flip_Flop d_ff_3 (.clk(clk), .D(In_4[2]), .Q(out4_d[2]), .en(w));  // open: Qn, preset, reset
  D_Flip_Flop d_ff_4 (.clk(clk), .D(In_4[3]), .Q(out4_d[3]), .en(w));  // open: Qn, preset, reset
  assign out[3] = en ? out4_d[3] : 1'bz;  // Controlled_Buffer controlled_buffer_1
  assign out[2] = en ? out4_d[2] : 1'bz;  // Controlled_Buffer controlled_buffer_2
  assign out[1] = en ? out4_d[1] : 1'bz;  // Controlled_Buffer controlled_buffer_3
  assign out[0] = en ? out4_d[0] : 1'bz;  // Controlled_Buffer controlled_buffer_4

  // Notes on the sheet:
  //   Registro 4b salida restringida
endmodule
