// Logisim project cpu.circ as structural Verilog: 1 circuit, main circuit main
module main (
);

  wire adder_1_cout, clock_1_out, unidad_de_control_1_alu1_in, unidad_de_control_1_alu2_in,
       unidad_de_control_1_aluadd, unidad_de_control_1_aluo_out, unidad_de_control_1_r0_in,
       unidad_de_control_1_r0_out, unidad_de_control_1_r1_in, unidad_de_control_1_r1_out,
       unidad_de_control_1_r2_in, unidad_de_control_1_r2_out, unidad_de_control_1_r3_in,
       unidad_de_control_1_r3_out;
  wire [7:0] adder_1_out, alu_in1_q, alu_in2_q, alu_out_q, controlled_buffer_1_out, R0_q, R1_q, R2_q, R3_q;

  Clock clock_1 (.out(clock_1_out));
  Register R0 (.D(controlled_buffer_1_out), .en(unidad_de_control_1_r0_in), .Q(R0_q), .clk(clock_1_out));  // open: clr
  Unidad_de_Control unidad_de_control_1 (
    .clk(clock_1_out), .R2_in(unidad_de_control_1_r2_in), .R0_in(unidad_de_control_1_r0_in),
    .R3_in(unidad_de_control_1_r3_in), .R1_in(unidad_de_control_1_r1_in),
    .ALU1_in(unidad_de_control_1_alu1_in), .ALU2_in(unidad_de_control_1_alu2_in),
    .R0_out(unidad_de_control_1_r0_out), .R1_out(unidad_de_control_1_r1_out),
    .R2_out(unidad_de_control_1_r2_out), .R3_out(unidad_de_control_1_r3_out),
    .ALUO_out(unidad_de_control_1_aluo_out), .ALUadd(unidad_de_control_1_aluadd));  // open: misteriosaOpX
  assign controlled_buffer_1_out = unidad_de_control_1_r0_out ? R0_q : 8'bz;  // Controlled_Buffer controlled_buffer_1
  Register R1 (.D(controlled_buffer_1_out), .en(unidad_de_control_1_r1_in), .Q(R1_q), .clk(clock_1_out));  // open: clr
  assign controlled_buffer_1_out = unidad_de_control_1_r1_out ? R1_q : 8'bz;  // Controlled_Buffer controlled_buffer_2
  Register R2 (.D(controlled_buffer_1_out), .en(unidad_de_control_1_r2_in), .Q(R2_q), .clk(clock_1_out));  // open: clr
  assign controlled_buffer_1_out = unidad_de_control_1_r2_out ? R2_q : 8'bz;  // Controlled_Buffer controlled_buffer_3
  Register R3 (.D(controlled_buffer_1_out), .en(unidad_de_control_1_r3_in), .Q(R3_q), .clk(clock_1_out));  // open: clr
  Register alu_in1 (
    .D(controlled_buffer_1_out), .en(unidad_de_control_1_alu1_in), .Q(alu_in1_q), .clk(clock_1_out));  // open: clr
  assign controlled_buffer_1_out = unidad_de_control_1_r3_out ? R3_q : 8'bz;  // Controlled_Buffer controlled_buffer_4
  Register alu_in2 (
    .D(controlled_buffer_1_out), .en(unidad_de_control_1_alu2_in), .Q(alu_in2_q), .clk(clock_1_out));  // open: clr
  Adder adder_1 (.a(alu_in1_q), .b(alu_in2_q), .out(adder_1_out), .cout(adder_1_cout));  // open: cin
  D_Flip_Flop Carry (
    .clk(clock_1_out), .D(adder_1_cout), .en(unidad_de_control_1_aluadd));  // open: Q, Qn, preset, reset
  Register alu_out (.D(adder_1_out), .en(unidad_de_control_1_aluadd), .Q(alu_out_q), .clk(clock_1_out));  // open: clr
  assign controlled_buffer_1_out = unidad_de_control_1_aluo_out ? alu_out_q : 8'bz;  // Controlled_Buffer controlled_buffer_5

  // Notes on the sheet:
  //   CLK
  //   Bus Interno (8 bits)
endmodule
