// Logisim project uc2.circ as structural Verilog: 1 circuit, main circuit Unidad de Control
module Unidad_de_Control (
  input  clk,
  output R0_in,
  output R1_in,
  output R2_in,
  output R3_in,
  output ALU1_in,
  output ALU2_in,
  output R0_out,
  output R1_out,
  output R2_out,
  output R3_out,
  output ALUO_out,
  output ALUadd,
  output misteriosaOpX
);

  wire decoder_1_out3;
  wire [3:0] Autoincrementador_q;
  wire [7:0] rom_1_data;

  Counter #(.width(4), .max('hf), .trigger("falling")) Autoincrementador (
    .Q(Autoincrementador_q), .clk(clk));  // open: load, D, count, carry, clr
  ROM #(.addrWidth(4)) rom_1 (.addr(Autoincrementador_q), .data(rom_1_data));  // open: sel
  Decoder #(.select(2), .disabled(0), .enable("false")) decoder_1 (
    .out1(misteriosaOpX), .out2(ALUadd), .out3(decoder_1_out3), .sel(rom_1_data[7:6]));  // open: out0
  Decoder #(.select(3), .disabled(0)) decoder_2 (
    .out0(R0_in), .out1(R1_in), .out2(R2_in), .out3(R3_in), .out4(ALU1_in), .out5(ALU2_in),
    .sel(rom_1_data[5:3]), .en(decoder_1_out3));  // open: out6, out7
  Decoder #(.select(3), .disabled(0)) decoder_3 (
    .out0(R0_out), .out1(R1_out), .out2(R2_out), .out3(R3_out), .out4(ALUO_out), .sel(rom_1_data[2:0]),
    .en(decoder_1_out3));  // open: out5, out6, out7

  // Notes on the sheet:
  //   Microprograma
endmodule
